// Logisim project Conway.circ as structural Verilog: 4 circuits, main circuit conway_cell
module conway_cell (
  input  Set_D_In,
  input  Row,
  input  Column,
  input  Lock,
  input  Btn,
  input  N1,
  input  N2,
  input  N3,
  input  N4,
  input  N5,
  input  N6,
  input  N7,
  input  N8,
  output Read_D_Out,
  output State_Out
);

  wire adder_1_cout, adder_1_out, adder_2_cout, adder_2_out, adder_3_cout, adder_3_out, adder_4_cout,
       adder_4_out, adder_5_cout, adder_5_out, adder_6_cout, adder_6_out, adder_7_cout, adder_7_out,
       adder_8_cout, adder_8_out, adder_9_cout, adder_9_out, adder_10_cout, adder_10_out, adder_11_cout,
       adder_11_out, clock_1_out, D_In_q, D_Out_q, D_Out_qn, eq_1_e3, eq_1_ne2, inner_logic_1_d_in_d,
       inner_logic_1_d_in_e, inner_logic_1_d_out_d, inner_logic_1_d_out_e;

  Clock clock_1 (.out(clock_1_out));
  Adder #(.width(1)) adder_1 (.a(N1), .b(N2), .out(adder_1_out), .cout(adder_1_cout));  // open: cin
  Adder #(.width(1)) adder_2 (.a(N3), .b(N4), .out(adder_2_out), .cout(adder_2_cout));  // open: cin
  Adder #(.width(1)) adder_3 (.a(N5), .b(N6), .out(adder_3_out), .cout(adder_3_cout));  // open: cin
  Adder #(.width(1)) adder_4 (.a(N7), .b(N8), .out(adder_4_out), .cout(adder_4_cout));  // open: cin
  Adder #(.width(1)) adder_5 (.a(adder_1_out), .b(adder_2_out), .out(adder_5_out), .cout(adder_5_cout));  // open: cin
  Adder #(.width(1)) adder_6 (
    .a(adder_1_cout), .b(adder_2_cout), .out(adder_6_out), .cin(adder_5_cout), .cout(adder_6_cout));
  Adder #(.width(1)) adder_7 (.a(adder_3_out), .b(adder_4_out), .out(adder_7_out), .cout(adder_7_cout));  // open: cin
  Adder #(.width(1)) adder_8 (
    .a(adder_3_cout), .b(adder_4_cout), .out(adder_8_out), .cin(adder_7_cout), .cout(adder_8_cout));
  Adder #(.width(1)) adder_9 (.a(adder_5_out), .b(adder_7_out), .out(adder_9_out), .cout(adder_9_cout));  // open: cin
  Adder #(.width(1)) adder_10 (
    .a(adder_6_out), .b(adder_8_out), .out(adder_10_out), .cin(adder_9_cout), .cout(adder_10_cout));
  Adder #(.width(1)) adder_11 (
    .a(adder_6_cout), .b(adder_8_cout), .out(adder_11_out), .cin(adder_10_cout), .cout(adder_11_cout));
  inner_logic inner_logic_1 (
    .Set_D_In(Set_D_In), .Row(Row), .Column(Column), .D_Out_Q(D_Out_q), .NE2(eq_1_ne2), .E3(eq_1_e3),
    .Clock(clock_1_out), .D_Out_Q_Comp(D_Out_qn), .Lock(Lock), .Btn(Btn), .D_In_Q(D_In_q),
    .Read_D_Out(Read_D_Out), .State_Out(State_Out), .D_In_D(inner_logic_1_d_in_d),
    .D_In_E(inner_logic_1_d_in_e), .D_Out_E(inner_logic_1_d_out_e), .D_Out_D(inner_logic_1_d_out_d));
  LED led_1 (.in(State_Out));
  D_Flip_Flop D_Out (
    .D(inner_logic_1_d_out_d), .clk(inner_logic_1_d_out_e), .Q(D_Out_q), .Qn(D_Out_qn));  // open: preset, reset
  eq eq_1 (
    .A_LeastSig(adder_9_out), .B(adder_10_out), .C(adder_11_out), .D_MostSig(adder_11_cout), .NE2(eq_1_ne2),
    .E3(eq_1_e3));
  D_Flip_Flop D_In (.D(inner_logic_1_d_in_d), .clk(inner_logic_1_d_in_e), .Q(D_In_q));  // open: Qn, preset, reset
endmodule

module inner_logic (
  input  Set_D_In,
  input  Row,
  input  Column,
  input  D_Out_Q,
  input  NE2,
  input  E3,
  input  Clock,
  input  D_Out_Q_Comp,
  input  Lock,
  input  Btn,
  input  D_In_Q,
  output Read_D_Out,
  output State_Out,
  output D_In_D,
  output D_In_E,
  output D_Out_E,
  output D_Out_D
);

  wire and_1_out, and_2_out, and_3_out, and_4_out, and_5_out, and_6_out, and_8_out, and_9_out, and_10_out,
       and_11_out, and_12_out, and_13_out, and_14_out, and_15_out, and_16_out, and_17_out, nand_1_out,
       nand_2_out, not_1_out, not_2_out, not_3_out, or_1_out, or_2_out, or_3_out;

  not not_1 (not_1_out, Clock);
  not not_2 (not_2_out, Lock);
  not not_3 (not_3_out, Btn);
  and and_1 (and_1_out, Row, Column);
  and and_2 (and_2_out, D_Out_Q_Comp, not_2_out);
  and and_3 (and_3_out, E3, Lock);
  and and_4 (and_4_out, NE2, not_1_out);
  and and_5 (and_5_out, Clock, Lock);
  and and_6 (and_6_out, not_3_out, not_2_out);
  and and_7 (Read_D_Out, and_1_out, D_Out_Q);
  and and_8 (and_8_out, Row, Column);
  nand nand_1 (nand_1_out, Row, Column);
  or or_1 (or_1_out, and_2_out, and_3_out);
  and and_9 (and_9_out, and_4_out, Lock);
  and and_10 (and_10_out, not_2_out, Btn);
  and and_11 (and_11_out, Row, Column);
  nand nand_2 (nand_2_out, Row, Column);
  or or_2 (or_2_out, and_5_out, and_6_out);
  and and_12 (and_12_out, Row, Column);
  and and_13 (and_13_out, and_8_out, Set_D_In);
  and and_14 (and_14_out, nand_1_out, or_1_out);
  or or_3 (or_3_out, and_9_out, and_10_out);
  and and_15 (and_15_out, and_11_out, Clock);
  and and_16 (and_16_out, nand_2_out, or_2_out);
  and and_17 (and_17_out, and_12_out, not_1_out);
  or or_4 (D_In_D, and_13_out, and_14_out);
  or or_5 (D_In_E, or_3_out, and_15_out);
  or or_6 (D_Out_E, and_16_out, and_17_out);

  assign D_Out_D = D_In_Q;
  assign State_Out = D_Out_Q;
endmodule

module eq (
  input  A_LeastSig,
  input  B,
  input  C,
  input  D_MostSig,
  output NE2,
  output E3
);

  wire and_1_out, and_2_out, nor_1_out, not_1_out;

  nor nor_1 (nor_1_out, C, D_MostSig);
  not not_1 (not_1_out, A_LeastSig);
  and and_1 (and_1_out, not_1_out, B);
  and and_2 (and_2_out, A_LeastSig, B);
  nand nand_1 (NE2, and_1_out, nor_1_out);
  and and_3 (E3, and_2_out, nor_1_out);
endmodule

module board_test (
);

  wire Column_sw1, Column_sw2, Column_sw3, conway_cell_1_state_out, conway_cell_2_state_out,
       conway_cell_3_state_out, conway_cell_4_state_out, conway_cell_5_state_out, conway_cell_6_state_out,
       conway_cell_7_state_out, conway_cell_8_state_out, conway_cell_9_state_out, conway_cell_10_state_out,
       D_In_sw1, Lock_sw1, Row_sw1, Row_sw2, Row_sw3, undriven, undriven_2, undriven_3, undriven_4;

  conway_cell conway_cell_1 (
    .Set_D_In(undriven_4), .Row(undriven_3), .Column(undriven_2), .Lock(undriven),
    .State_Out(conway_cell_1_state_out));  // open: Btn, N1, N2, N3, N4, N5, N6, N7, N8, Read_D_Out
  LED led_1 (.in(conway_cell_1_state_out));
  DipSwitch #(.number(3)) Row (.sw1(Row_sw1), .sw2(Row_sw2), .sw3(Row_sw3));
  DipSwitch #(.number(3)) Column (.sw1(Column_sw1), .sw2(Column_sw2), .sw3(Column_sw3));
  DipSwitch #(.number(1)) Lock (.sw1(Lock_sw1));
  conway_cell conway_cell_2 (
    .Set_D_In(D_In_sw1), .Row(Row_sw1), .Column(Column_sw1), .Lock(Lock_sw1), .Btn(conway_cell_5_state_out),
    .N1(conway_cell_3_state_out), .N2(conway_cell_6_state_out), .State_Out(conway_cell_2_state_out));  // open: N3, N4, N5, N6, N7, N8, Read_D_Out
  conway_cell conway_cell_3 (
    .Set_D_In(D_In_sw1), .Row(Row_sw2), .Column(Column_sw1), .Lock(Lock_sw1), .Btn(conway_cell_6_state_out),
    .N1(conway_cell_4_state_out), .N2(conway_cell_7_state_out), .N5(conway_cell_2_state_out),
    .N7(conway_cell_5_state_out), .State_Out(conway_cell_3_state_out));  // open: N3, N4, N6, N8, Read_D_Out
  conway_cell conway_cell_4 (
    .Set_D_In(D_In_sw1), .Row(Row_sw3), .Column(Column_sw1), .Lock(Lock_sw1), .Btn(conway_cell_7_state_out),
    .N5(conway_cell_3_state_out), .N7(conway_cell_6_state_out), .State_Out(conway_cell_4_state_out));  // open: N1, N2, N3, N4, N6, N8, Read_D_Out
  DipSwitch #(.number(1)) D_In (.sw1(D_In_sw1));
  LED led_2 (.in(conway_cell_2_state_out));
  LED led_3 (.in(conway_cell_3_state_out));
  LED led_4 (.in(conway_cell_4_state_out));
  conway_cell conway_cell_5 (
    .Set_D_In(D_In_sw1), .Row(Row_sw1), .Column(Column_sw2), .Lock(Lock_sw1), .Btn(conway_cell_8_state_out),
    .N1(conway_cell_6_state_out), .N2(conway_cell_9_state_out), .N3(conway_cell_3_state_out),
    .N4(conway_cell_2_state_out), .State_Out(conway_cell_5_state_out));  // open: N5, N6, N7, N8, Read_D_Out
  conway_cell conway_cell_6 (
    .Set_D_In(D_In_sw1), .Row(Row_sw2), .Column(Column_sw2), .Lock(Lock_sw1), .Btn(conway_cell_9_state_out),
    .N1(conway_cell_7_state_out), .N2(conway_cell_10_state_out), .N3(conway_cell_4_state_out),
    .N4(conway_cell_3_state_out), .N5(conway_cell_5_state_out), .N6(conway_cell_2_state_out),
    .N7(conway_cell_8_state_out), .State_Out(conway_cell_6_state_out));  // open: N8, Read_D_Out
  conway_cell conway_cell_7 (
    .Set_D_In(D_In_sw1), .Row(Row_sw3), .Column(Column_sw2), .Lock(Lock_sw1), .Btn(conway_cell_10_state_out),
    .N4(conway_cell_4_state_out), .N5(conway_cell_6_state_out), .N6(conway_cell_3_state_out),
    .N7(conway_cell_9_state_out), .State_Out(conway_cell_7_state_out));  // open: N1, N2, N3, N8, Read_D_Out
  LED led_5 (.in(conway_cell_5_state_out));
  LED led_6 (.in(conway_cell_6_state_out));
  LED led_7 (.in(conway_cell_7_state_out));
  conway_cell conway_cell_8 (
    .Set_D_In(D_In_sw1), .Row(Row_sw1), .Column(Column_sw3), .Lock(Lock_sw1), .N1(conway_cell_9_state_out),
    .N2(conway_cell_6_state_out), .N4(conway_cell_5_state_out), .State_Out(conway_cell_8_state_out));  // open: Btn, N3, N5, N6, N7, N8, Read_D_Out
  conway_cell conway_cell_9 (
    .Set_D_In(D_In_sw1), .Row(Row_sw2), .Column(Column_sw3), .Lock(Lock_sw1), .N1(conway_cell_10_state_out),
    .N3(conway_cell_7_state_out), .N4(conway_cell_6_state_out), .N5(conway_cell_8_state_out),
    .N6(conway_cell_5_state_out), .State_Out(conway_cell_9_state_out));  // open: Btn, N2, N7, N8, Read_D_Out
  conway_cell conway_cell_10 (
    .Set_D_In(D_In_sw1), .Row(Row_sw3), .Column(Column_sw3), .Lock(Lock_sw1), .N4(conway_cell_7_state_out),
    .N5(conway_cell_9_state_out), .N6(conway_cell_6_state_out), .State_Out(conway_cell_10_state_out));  // open: Btn, N1, N2, N3, N7, N8, Read_D_Out
  LED led_8 (.in(conway_cell_8_state_out));
  LED led_9 (.in(conway_cell_9_state_out));
  LED led_10 (.in(conway_cell_10_state_out));
endmodule
